# Fritzing sketch FlexRigShield (saved by Fritzing 0.8.7b)
circuit board: 9.92681cm x 5.94347cm
breadboards: 1

parts:
  R3 = Resistor [tolerance=±5% resistance=1M power=0.25 package=THT]
  R4 = Resistor [tolerance=±5% resistance=1M power=0.25 package=THT]
  R5 = Resistor [tolerance=±5% resistance=1M power=0.25 package=THT]
  R6 = Resistor [tolerance=±5% resistance=1M power=0.25 package=THT]
  R23 = Resistor [tolerance=±5% resistance=1M power=0.25 package=THT]
  R10 = Resistor [tolerance=±5% resistance=1M power=0.25 package=THT]
  R11 = Resistor [tolerance=±5% resistance=1M power=0.25 package=THT]
  R12 = Resistor [tolerance=±5% resistance=1M power=0.25 package=THT]
  FMHD11 = female pin header, 6 pins [form="♀ (female)"]
  FMHD12 = female pin header, 6 pins [form="♀ (female)"]  # not connected
  FMHD13 = female pin header, 8 pins [form="♀ (female)"]
  FMHD14 = female pin header, 8 pins [form="♀ (female)"]
  R24 = Resistor [tolerance=±5% resistance=1M power=0.25 package=THT]
  F1 = female pin header, 2 pins [form="♀ (female)"]
  F2 = female pin header, 2 pins [form="♀ (female)"]
  F3 = female pin header, 2 pins [form="♀ (female)"]
  F4 = female pin header, 2 pins [form="♀ (female)"]
  F6 = female pin header, 2 pins [form="♀ (female)"]
  F7 = female pin header, 2 pins [form="♀ (female)"]
  H-bridge2 = H-Bridge [package=THT]
  H-bridge1 = H-Bridge [package=THT]
  R21 = Resistor [tolerance=±5% resistance=1M power=0.25 package=THT]
  R22 = Resistor [tolerance=±5% resistance=1M power=0.25 package=THT]
  JP1 = FTDI_BASIC [package=ftdi_basic]
  JP2 = FTDI_BASIC [package=ftdi_basic]
  R25 = Resistor [tolerance=±5% power=0.25 resistance=100k package=THT]
  F8 = female pin header, 2 pins [form="♀ (female)"]
  reset = SWITCH-MOMENTARY-2 [package=tactile-switch-1101ne]
  FMHD15 = female pin header, 8 pins [form="♀ (female)"]
  FMHD16 = double row female pin header, 36 pins [form="♀ (female)"]
  FMHD17 = female pin header, 8 pins [form="♀ (female)"]  # not connected
  F9 = female pin header, 2 pins [form="♀ (female)"]

nets:
  GND1: R3.Pin_0, R4.Pin_0, R5.Pin_0, R6.Pin_0, R10.Pin_0, R11.Pin_0, R12.Pin_0, FMHD11.pin2, R24.Pin_0, F1.pin2, F2.pin2, F3.pin2, F4.pin2, F6.pin2, F7.pin2, H-bridge2.GND1, H-bridge2.GND2, H-bridge2.GND3, H-bridge2.GND4, H-bridge1.GND1, H-bridge1.GND2, H-bridge1.GND3, H-bridge1.GND4, R21.Pin_1, R22.Pin_1, R25.Pin_1, reset.1
  N1: R3.Pin_1, FMHD14.pin2, H-bridge1.2A
  N2: R4.Pin_1, FMHD13.pin8, H-bridge2.3A
  N3: R5.Pin_1, FMHD13.pin6, H-bridge2.1A
  N4: R6.Pin_1, FMHD13.pin5, H-bridge2.4A
  N5: R23.Pin_1, JP2.2
  N6: R10.Pin_1, FMHD14.pin3, H-bridge1.1A
  N7: R11.Pin_1, FMHD13.pin7
  N8: R12.Pin_1, FMHD14.pin1, H-bridge1.4A
  N9: FMHD11.pin1, FMHD16.pin1
  N10: FMHD11.pin3, FMHD15.pin5
  N11: FMHD11.pin4, FMHD15.pin6
  N12: FMHD14.pin4, R24.Pin_1
  N13: FMHD14.pin5, H-bridge2.2A
  N14: FMHD14.pin6, H-bridge1.3A
  N15: F1.pin1, H-bridge2.4Y
  N16: F2.pin1, H-bridge2.1Y
  N17: F3.pin1, H-bridge2.3Y
  N18: F4.pin1, H-bridge1.1Y
  N19: F6.pin1, H-bridge1.4Y
  N20: F7.pin1, H-bridge1.2Y
  N21: H-bridge2.1_2EN, H-bridge2.VCC1, H-bridge1.1_2EN, H-bridge1.VCC1, JP2.3
  N22: H-bridge2.2Y, F9.pin2
  N23: H-bridge2.VCC2, H-bridge1.VCC2, JP2.6
  N24: H-bridge2.3_4EN, H-bridge1.3_4EN
  N25: H-bridge1.3Y, F9.pin1
  N26: R21.Pin_0, JP1.6
  N27: R22.Pin_0, JP1.1
  N28: JP2.1, reset.2
  N29: R25.Pin_0, F8.pin1
