# Fritzing sketch SIR Shield 1 (saved by Fritzing 0.9.10b)
circuit board: 9.84324cm x 6.53cm
breadboards: 1

parts:
  R3 = Resistor [tolerance=±5% resistance=1M power=0.25 package=THT]
  R4 = Resistor [tolerance=±5% resistance=1M power=0.25 package=THT]
  R5 = Resistor [tolerance=±5% resistance=1M power=0.25 package=THT]
  R6 = Resistor [tolerance=±5% resistance=1M power=0.25 package=THT]
  R23 = Resistor [tolerance=±5% resistance=1M power=0.25 package=THT]
  R10 = Resistor [tolerance=±5% resistance=1M power=0.25 package=THT]
  R11 = Resistor [tolerance=±5% resistance=1M power=0.25 package=THT]
  R12 = Resistor [tolerance=±5% resistance=1M power=0.25 package=THT]
  FMHD11 = female pin header, 6 pins [form="♀ (female)"]
  FMHD12 = female pin header, 6 pins [form="♀ (female)"]
  FMHD13 = female pin header, 8 pins [form="♀ (female)"]
  FMHD14 = female pin header, 8 pins [form="♀ (female)"]
  R24 = Resistor [tolerance=±5% resistance=1M power=0.25 package=THT]
  F1 = female pin header, 2 pins [form="♀ (female)"]
  F2 = female pin header, 2 pins [form="♀ (female)"]
  F3 = female pin header, 2 pins [form="♀ (female)"]
  F4 = female pin header, 2 pins [form="♀ (female)"]
  F5 = female pin header, 2 pins [form="♀ (female)"]
  F6 = female pin header, 2 pins [form="♀ (female)"]
  F7 = female pin header, 2 pins [form="♀ (female)"]
  H-bridge2 = H-Bridge [package=THT]
  H-bridge1 = H-Bridge [package=THT]
  R21 = Resistor [tolerance=±5% resistance=1M power=0.25 package=THT]
  R22 = Resistor [tolerance=±5% resistance=1M power=0.25 package=THT]
  JP1 = FTDI_BASIC [package=ftdi_basic]
  JP2 = FTDI_BASIC [package=ftdi_basic]
  R25 = Resistor [tolerance=±5% power=0.25 resistance=100k package=THT]
  F8 = female pin header, 2 pins [form="♀ (female)"]
  reset = SWITCH-MOMENTARY-2 [package=tactile-switch-1101ne]
  J1 = Power Jack [package=power_jack_slot]
  J2 = female pin header, 4 pins [form="♀ (female)"]
  R26 = Resistor [tolerance=±5% power=0.25 resistance=100k package=THT]
  R27 = Resistor [tolerance=±5% power=0.25 resistance=680 package=THT]
  D1 = Rectifier Diode [part_number=1N4001 package="300 mil [THT]"]
  FMHD15 = female pin header, 8 pins [form="♀ (female)"]
  FMHD16 = double row female pin header, 36 pins [form="♀ (female)"]
  FMHD17 = female pin header, 8 pins [form="♀ (female)"]  # not connected
  FMHD18 = female pin header, 10 pins [form="♀ (female)"]
  C1_Ground = Electrolytic Capacitor [capacitance=1µF voltage=35V package="100 mil [THT, electrolytic]"]
  C2_Rin = Electrolytic Capacitor [capacitance=1µF voltage=35V package="100 mil [THT, electrolytic]"]
  C3_Lin = Electrolytic Capacitor [capacitance=1µF voltage=35V package="100 mil [THT, electrolytic]"]
  J3 = female pin header, 1 pin [form="♀ (female)"]
  J3_2 = female pin header, 1 pin [form="♀ (female)"]
  J4 = female pin header, 1 pin [form="♀ (female)"]

nets:
  GND1: R3.Pin_0, R4.Pin_0, R5.Pin_0, R6.Pin_0, R10.Pin_0, R11.Pin_0, R12.Pin_0, FMHD11.pin2, R24.Pin_0, F1.pin2, F2.pin2, F3.pin2, F4.pin2, F5.pin2, F6.pin2, F7.pin2, H-bridge2.GND1, H-bridge2.GND2, H-bridge2.GND3, H-bridge2.GND4, H-bridge1.GND1, H-bridge1.GND2, H-bridge1.GND3, H-bridge1.GND4, R21.Pin_1, R22.Pin_1, JP2.4, R25.Pin_1, reset.1
  N1: R3.Pin_1, FMHD14.pin2, H-bridge1.3A
  N2: R4.Pin_1, FMHD13.pin8, H-bridge2.3A
  N3: R5.Pin_1, FMHD13.pin6, H-bridge2.1A
  N4: R6.Pin_1, H-bridge2.4A
  N5: R23.Pin_1, JP2.2
  N6: R10.Pin_1, FMHD14.pin3, H-bridge1.1A
  N7: R11.Pin_1, FMHD13.pin7, H-bridge2.2A
  N8: R12.Pin_1, FMHD14.pin1, H-bridge1.4A
  N9: FMHD11.pin1, FMHD16.pin1, FMHD18.pin1, FMHD18.pin10
  N10: FMHD11.pin3, FMHD15.pin5
  N11: FMHD11.pin4, FMHD15.pin6
  N12: FMHD11.pin5, C2_Rin.-
  N13: FMHD11.pin6, C3_Lin.-
  N14: FMHD12.pin3, FMHD14.pin5, J4.pin1
  N15: FMHD12.pin4, FMHD14.pin6, J3.pin1
  N16: FMHD12.pin6, FMHD14.pin7, J3_2.pin1
  N17: FMHD13.pin2, J2.pin4, R26.Pin_0, FMHD18.pin2, C1_Ground.-
  N18: FMHD13.pin3, R27.Pin_0
  N19: FMHD13.pin4, D1.anode
  N20: FMHD14.pin4, R24.Pin_1, H-bridge1.2A
  N21: F1.pin1, H-bridge2.4Y
  N22: F2.pin1, H-bridge2.1Y
  N23: F3.pin1, H-bridge2.3Y
  N24: F4.pin1, H-bridge1.1Y
  N25: F5.pin1, H-bridge1.2Y
  N26: F6.pin1, H-bridge1.4Y
  N27: F7.pin1, H-bridge1.3Y
  N28: H-bridge2.1_2EN, H-bridge2.VCC1, H-bridge1.1_2EN, H-bridge1.VCC1, JP2.3
  N29: H-bridge2.VCC2, H-bridge1.VCC2, JP2.6
  N30: H-bridge2.3_4EN, H-bridge1.3_4EN
  N31: R21.Pin_0, JP1.6
  N32: R22.Pin_0, JP1.1
  N33: JP2.1, reset.2
  N34: R25.Pin_0, F8.pin1
  N35: J1.GNDBREAK, J2.pin1
  N36: J1.PWR, J2.pin2
  N37: J2.pin3, R26.Pin_1, R27.Pin_1, D1.cathode
  N38: FMHD15.pin7, FMHD18.pin9
  N39: FMHD15.pin8, FMHD18.pin8
  N40: FMHD18.pin4, FMHD18.pin7, C1_Ground.+
  N41: FMHD18.pin5, C2_Rin.+
  N42: FMHD18.pin6, C3_Lin.+
